// Logisim project 4BitCPU.circ as structural Verilog: 1 circuit, main circuit main
module main (
  input  write,
  input  [1:0] srcreg,
  input  [1:0] destreg,
  input  [3:0] data,
  output [3:0] out_5,
  output [3:0] srcreg_val,
  output [3:0] destreg_val
);

  wire and_1_out, and_2_out, and_3_out, and_4_out, and_5_out, and_6_out, and_7_out, and_8_out, clock_1_out,
       not_1_out, not_2_out, not_3_out, not_4_out;
  wire [3:0] register_1_q, register_2_q, register_3_q, register_4_q;

  Clock clock_1 (.out(clock_1_out));
  not not_1 (not_1_out, destreg[0]);
  not not_2 (not_2_out, destreg[1]);
  not not_3 (not_3_out, destreg[1]);
  not not_4 (not_4_out, destreg[0]);
  and and_1 (and_1_out, write, and_2_out);
  and and_2 (and_2_out, not_1_out, not_2_out);
  and and_3 (and_3_out, write, and_4_out);
  and and_4 (and_4_out, destreg[0], not_3_out);
  and and_5 (and_5_out, write, and_6_out);
  and and_6 (and_6_out, not_4_out, destreg[1]);
  and and_7 (and_7_out, write, and_8_out);
  and and_8 (and_8_out, destreg[0], destreg[1]);
  Register #(.width(4)) register_1 (.D(data), .en(and_1_out), .clk(clock_1_out), .Q(register_1_q));  // open: clr
  Register #(.width(4)) register_2 (.D(data), .en(and_3_out), .clk(clock_1_out), .Q(register_2_q));  // open: clr
  Register #(.width(4)) register_3 (.D(data), .en(and_5_out), .clk(clock_1_out), .Q(register_3_q));  // open: clr
  Register #(.width(4)) register_4 (.D(data), .en(and_7_out), .clk(clock_1_out), .Q(register_4_q));  // open: clr
  Multiplexer #(.select(2), .width(4)) multiplexer_1 (
    .in0(register_1_q), .in1(register_2_q), .in2(register_3_q), .in3(register_4_q), .out(srcreg_val),
    .sel(srcreg));
  Multiplexer #(.select(2), .width(4)) multiplexer_2 (
    .in0(register_1_q), .in1(register_2_q), .in2(register_3_q), .in3(register_4_q), .out(destreg_val),
    .sel(destreg));
  Adder #(.width(4)) adder_1 (.a(srcreg_val), .b(destreg_val), .out(out_5));  // open: cin, cout
  Shifter shifter_1 ();  // open: in, dist, out
  // MinMax minmax_1: pin names not known
  Comparator comparator_1 ();  // open: a, b, gt, eq, lt
  Subtractor #(.width(4)) subtractor_1 ();  // open: a, b, out, bin, bout
  Divider divider_1 ();  // open: a, b, out, upper, rem
  Negator negator_1 ();  // open: in, out
  // Exponentiator exponentiator_1: pin names not known
  // SquareRoot squareroot_1: pin names not known
  // Absolute absolute_1: pin names not known
endmodule
